# Fritzing sketch ProjectCircuit (saved by Fritzing 0.9.2b)
breadboards: 3

parts:
  Part1 = Arduino Micro (Rev3)  # not connected
  R3 = Resistor [tolerance=±5% resistance=560 package=THT]
  R8 = Resistor [tolerance=±5% resistance=560 package=THT]
  R9 = Resistor [tolerance=±5% resistance=560 package=THT]
  R10 = Resistor [tolerance=±5% resistance=560 package=THT]
  R11 = Resistor [tolerance=±5% resistance=560 package=THT]
  R12 = Resistor [tolerance=±5% resistance=560 package=THT]
  R13 = Resistor [tolerance=±5% resistance=560 package=THT]
  R14 = Resistor [tolerance=±5% resistance=560 package=THT]
  Part2 = Thumb Joystick
  S1 = Pushbutton [package=THT]
  S2 = Pushbutton [package=THT]
  S3 = Pushbutton [package=THT]
  S4 = Pushbutton [package=THT]
  S5 = Pushbutton [package=THT]
  S6 = Pushbutton [package=THT]
  S7 = Pushbutton [package=THT]
  S9 = Pushbutton [package=THT]

nets:
  N1: R3.Pin_0, R8.Pin_0, R9.Pin_0, R10.Pin_0, R11.Pin_0, R12.Pin_0, R13.Pin_0, R14.Pin_0, Part2.GND
  N2: R3.Pin_1, S7.leg0
  N3: R8.Pin_1, S6.leg1
  N4: R9.Pin_1, S5.leg1
  N5: R10.Pin_1, S4.leg1
  N6: R11.Pin_1, S3.leg1
  N7: R12.Pin_1, S2.leg1
  N8: R13.Pin_1, S1.leg1
  N9: R14.Pin_1, S9.leg0
  N10: Part2.VCC, S1.leg0, S2.leg0, S3.leg0, S4.leg0, S5.leg0, S6.leg0, S7.leg1, S9.leg1
